# Fritzing sketch Untitled Sketch (saved by Fritzing 0.9.3b)
breadboards: 1

parts:
  부품1 = Arduino Uno (Rev3)
  LED1 = RGB LED (com. cathode, rgb) [package="5 mm [THT]"]
  S1 = Pushbutton [package="[THT]"]
  S2 = Pushbutton [package="[THT]"]
  S3 = Pushbutton [package="[THT]"]
  R1 = Resistor [tolerance=±5% resistance=10k package=THT]
  R2 = Resistor [tolerance=±5% resistance=10k package=THT]
  R3 = Resistor [tolerance=±5% resistance=10k package=THT]
  J1 = Piezo Speaker
  LCD1 = LCD screen
  R4 = Rotary Potentiometer (Small) [maximum_resistance=10kΩ package=THT]

nets:
  N1: 부품1.A0, J1.pin2
  N2: 부품1.D8, S1.Pin_3, S1.Pin_4, R1.Pin_1
  N3: 부품1.D9_PWM, S3.Pin_3, S3.Pin_4, R3.Pin_1
  N4: 부품1.D10_PWM/SS, S2.Pin_3, S2.Pin_4, R2.Pin_1
  N5: 부품1.D11_PWM/MOSI, LED1.blue_anode
  N6: 부품1.D12/MISO, LED1.green_anode
  N7: 부품1.D13/SCK, LED1.common_cathode
  GND: 부품1.GND, LED1.red_anode, R1.Pin_0, R2.Pin_0, J1.pin1, LCD1.VSS, LCD1.LED-, R4.leg1
  N8: 부품1.D2, LCD1.DB4
  N9: 부품1.D3_PWM, LCD1.DB5
  N10: 부품1.D4, LCD1.DB6
  N11: 부품1.D5_PWM, LCD1.DB7
  N12: 부품1.D6_PWM, LCD1.E
  N13: 부품1.D7, LCD1.RS
  5V: 부품1.5V, S1.Pin_1, S1.Pin_2, S2.Pin_1, S2.Pin_2, S3.Pin_1, S3.Pin_2, LCD1.VDD, LCD1.R/W, LCD1.LED+, R4.leg2
  N14: LCD1.V0, R4.wiper
